# Fritzing sketch Arduino Push Button Switch (saved by Fritzing 0.9.3b)
breadboards: 1

parts:
  Part1 = Arduino Uno (Rev3)
  S1 = Pushbutton [package="[THT]"]

nets:
  N1: Part1.D8, S1.Pin_3, S1.Pin_4
  N2: Part1.3V3, S1.Pin_1, S1.Pin_2

// code stored in the sketch: Push_Button_Serial_monitor.ino
/*
 The Arduino should read the push button switch and print on the serial monitor the curent state. 1 for ON and 0 for off
 */
void setup()
{
  pinMode(8, INPUT);
  Serial.begin(9600);//This sets the baud rate of the serial monitor
  
}

void loop()
{
  
    if (digitalRead(8) == HIGH){
      Serial.println(1);    
  }else Serial.println(0);
  delay (100);          
  }
